// Logisim project P2.circ as structural Verilog: 8 circuits, main circuit Execute
module Execute (
  input  [31:0] ResultFromALURegister,
  input  [31:0] ResultFromFinalMux,
  input  [31:0] ReadD1,
  input  [31:0] ReadD2,
  input  [31:0] FromImmGen,
  input  WriteRegisterInstructionInput,
  input  ControlExecuteMux,
  input  [3:0] ControlOpCode,
  input  [4:0] ControlShiftAmount,
  input  Clock
);

  wire [1:0] forwardingunit_1_out_7, forwardingunit_1_out_8;
  wire [7:1] undriven;
  wire [31:0] alu_1_p6, multiplexer_1_out, multiplexer_2_out, multiplexer_3_out;

  Multiplexer #(.width(32), .enable("false")) multiplexer_1 (
    .in0(ReadD2), .in1(FromImmGen), .out(multiplexer_1_out), .sel(ControlExecuteMux));
  Multiplexer #(.select(2), .width(32), .enable("false")) multiplexer_2 (
    .in0(ReadD1), .in1(ResultFromFinalMux), .in2(ResultFromALURegister), .out(multiplexer_2_out),
    .sel(forwardingunit_1_out_8));  // open: in3
  Multiplexer #(.select(2), .width(32), .enable("false")) multiplexer_3 (
    .in0(multiplexer_1_out), .in1(ResultFromFinalMux), .in2(ResultFromALURegister), .out(multiplexer_3_out),
    .sel(forwardingunit_1_out_7));  // open: in3
  ForwardingUnit forwardingunit_1 (
    .out_7(forwardingunit_1_out_7), .out_8(forwardingunit_1_out_8));  // open: in_1, in_2, in_3, in_4, in_5, in_6
  // ALU alu_1: pin names not known; wires that end beside it: multiplexer_2_out, multiplexer_3_out, ControlOpCode, forwardingunit_1_out_7, ControlShiftAmount, alu_1_p6
  Register WB1 (.clk(Clock));  // open: D, en, Q, clr
  Register M1 (.clk(Clock));  // open: D, en, Q, clr
  Register #(.width(32)) Result (.D(alu_1_p6), .clk(Clock));  // open: en, Q, clr
  Register #(.width(32)) ReadData2 (.D(ReadD2), .clk(Clock));  // open: en, Q, clr
  Register WriteRegisterInstruction (.D({undriven, WriteRegisterInstructionInput}), .clk(Clock));  // open: en, Q, clr
  Register WB2 (.clk(Clock));  // open: D, en, Q, clr
  Register M2 (.clk(Clock));  // open: D, en, Q, clr
  Register M3 (.clk(Clock));  // open: D, en, Q, clr
  // Pins of 1 and 8 bits meet at {undriven, WriteRegisterInstructionInput}
endmodule

module Decode (
  input  Instruction,
  input  Clock
);

  wire immgen_1_out_2;
  wire [7:0] control_1_p2, control_1_p3, control_1_p4, control_1_p5, control_1_p6, control_1_p7,
       control_1_p8, registerfile_1_p1, registerfile_1_p2, undriven;

  // Control control_1: pin names not known; wires that end beside it: Instruction, control_1_p2, control_1_p3, control_1_p4, control_1_p5, control_1_p6, control_1_p7, control_1_p8
  // RegisterFile registerfile_1: pin names not known; wires that end beside it: registerfile_1_p1, registerfile_1_p2
  ImmGen immgen_1 (.out_2(immgen_1_out_2));  // open: in_1
  Register WB1 (.D(control_1_p2), .clk(Clock));  // open: en, Q, clr
  Register M1 (.D(control_1_p4), .clk(Clock));  // open: en, Q, clr
  Register EX1 (.D(control_1_p7), .clk(Clock));  // open: en, Q, clr
  Register ReadD1 (.D(registerfile_1_p1), .clk(Clock));  // open: en, Q, clr
  Register FromImmGen ();  // open: D, en, Q, clk, clr
  Register WriteRegisterInstruction (.D(undriven), .clk(Clock));  // open: en, Q, clr
  Register WB2 (.D(control_1_p3), .clk(Clock));  // open: en, Q, clr
  Register M2 (.D(control_1_p5), .clk(Clock));  // open: en, Q, clr
  Register EX2 (.D(control_1_p8), .clk(Clock));  // open: en, Q, clr
  Register ReadD2 (.D(registerfile_1_p2), .clk(Clock));  // open: en, Q, clr
  Register M3 (.D(control_1_p6), .clk(Clock));  // open: en, Q, clr
endmodule

module Control (
  input  Instruction,
  output WB1,
  output WB2,
  output M1,
  output M2,
  output M3,
  output EX1,
  output EX2
);


  // Notes on the sheet:
  //   Control
endmodule

module ImmGen (
  input  in_1,
  output out_2
);


  assign out_2 = in_1;

  // Notes on the sheet:
  //   Imm Gen
endmodule

module Fetch (
  input  Reset,
  input  Clock,
  output [31:0] Instruction
);

  wire [31:0] PC_q, risc_vprogramrom_1_p1;
  wire [31:2] PC_q_2;

  Register #(.width(32)) PC (.D(PC_q), .clk(Clock), .Q({PC_q_2, PC_q[1:0]}), .clr(Reset));  // open: en
  // Incrementer #(.width(30)) incrementer_1: pin names not known; wires that end beside it: {PC_q_2, PC_q[1:0]}, PC_q_2, PC_q[31:2]
  // RISC_VProgramROM risc_vprogramrom_1: pin names not known; wires that end beside it: risc_vprogramrom_1_p1
  Register #(.width(32)) InstructionRegister (
    .D(risc_vprogramrom_1_p1), .clk(Clock), .Q(Instruction));  // open: en, clr

  // Notes on the sheet:
  //   For some reason the registers were not working until I added zeros, no clue why just commenting in case we run into trouble later with it
endmodule

module Memory (
  input  ControlMemWrite,
  input  [31:0] ResultAddress,
  input  [31:0] ReadD2,
  input  WriteRegisterInstruction,
  input  ControlMemRead,
  output [31:0] ReadData,
  output [31:0] ResultAddressRegister,
  output WriteRegisterInstructionRegister
);

  Register WB1 ();  // open: D, en, Q, clk, clr
  Register register_1 ();  // open: D, en, Q, clk, clr
  Register register_2 ();  // open: D, en, Q, clk, clr
  Register register_3 ();  // open: D, en, Q, clk, clr
  Register WB2 ();  // open: D, en, Q, clk, clr

  // Notes on the sheet:
  //   This stage is just a pass through that does nothing
endmodule

module WriteBack (
  input  [31:0] ReadD,
  input  [31:0] Address,
  input  ControlMemtoReg,
  input  Clock,
  output [31:0] WriteData
);

  wire [31:0] multiplexer_1_out;

  Multiplexer #(.width(32), .enable("false")) multiplexer_1 (
    .in0(ReadD), .in1(Address), .out(multiplexer_1_out), .sel(ControlMemtoReg));
  Register #(.width(32)) WriteDataRegister (.D(multiplexer_1_out), .clk(Clock), .Q(WriteData));  // open: en, clr
endmodule

module ForwardingUnit (
  input  in_1,
  input  in_2,
  input  in_3,
  input  in_4,
  input  in_5,
  input  in_6,
  output [1:0] out_7,
  output [1:0] out_8
);
endmodule
